# Fritzing sketch 40_pin_BoosterPack_template (saved by Fritzing 0.8.3b)
breadboards: 1

parts:
  J1 = male pin header, 10 pins [form="♂ (male)"]  # not connected
  J3 = male pin header, 10 pins [form="♂ (male)"]
  J4 = male pin header, 10 pins [form="♂ (male)"]  # not connected
  J2 = male pin header, 10 pins [form="♂ (male)"]

nets:
  GND: J3.pin9, J2.pin10

notes:
  Outside 20 pins
  Inside 20 pins
  J1
  J2
  J3
  J4
  3V3
  Analog In
  RESERVED
  GND
  UART RX (>>MCU)
  UART TX (<<MCU)
  SPI CLK
  GPIO (!)
  I2C SCL
  I2C SDA
  5V
  PWM out / GPIO (!)
  SPI CS Wireless / GPIO (!)
  SPI CS Display / GPIO (!)
  SPI CS Other / GPIO (!)
  RST
  SPI MOSI
  SPI MISO
  Timer Capture / GPIO (!)
  Find more info @ www.ti.com/byob
  1
  21
  40
  20
  10
  11
  30
  31
